# Fritzing sketch sketch (saved by Fritzing 0.8.5b)

parts:
  Part1 = Arduino Uno (Rev3)
  SPKR1 = Loudspeaker
  R1 = Resistor [tolerance=±5% resistance=220 package=THT]

nets:
  N1: Part1.GND, SPKR1.pin1
  N2: Part1.D3_PWM, R1.Pin_0
  N3: SPKR1.pin2, R1.Pin_1
